# Fritzing sketch IAS-Sensor2 (saved by Fritzing 1.0.0rc)
circuit board: 5.78347cm x 2.58051cm
breadboards: 1

parts:
  S1 = Pushbutton [package="[THT]"]
  LED1 = LED - 5mm [color="Red (633nm)" current=0.030A package="5 mm [THT]"]
  U1 = LIPO-1000mAh [package=lipo-1000]
  AMS_5915 = AD22151 - Linear Output Magnetic Field Sensor [part_number=AD22151]
  MS5611 = MPL3115A2 [package=lga8]
  S2 = Pushbutton [package="[THT]"]
  R4 = Resistor [tolerance=±5% resistance=4.7k power=0.25W package="0603 [SMD]"]
  R3 = Resistor [tolerance=±5% resistance=4.7k power=0.25W package="0603 [SMD]"]
  R1 = Resistor [tolerance=±5% resistance=220 power=0.25W package="0603 [SMD]"]
  R2 = Resistor [tolerance=±5% resistance=4.7k power=0.25W package="0603 [SMD]"]
  R5 = Resistor [tolerance=±5% resistance=4.7k power=0.25W package="0603 [SMD]"]
  R6 = Resistor [tolerance=±5% resistance=4.7k power=0.25W package="0603 [SMD]"]
  R7 = Resistor [tolerance=±5% resistance=4.7k power=0.25W package="0603 [SMD]"]
  MCU1 = Wemos Lolin32lite
  C1 = Ceramic Capacitor [capacitance=100nF voltage=16V package="1206 [SMD, multilayer]"]

nets:
  N1: S1.Pin_1, S1.Pin_2, S2.Pin_1, S2.Pin_2, MCU1.pin_28
  N2: S1.Pin_3, S1.Pin_4, R2.Pin_1, MCU1.pin_4
  GND: LED1.cathode, AMS_5915.GND, MS5611.GND, MS5611.SCB, MS5611.INT2, R2.Pin_0, R5.Pin_0, R6.Pin_0, MCU1.pin_13, C1.1
  N3: LED1.anode, R1.Pin_0
  N4: U1.+, R7.Pin_0
  N5: AMS_5915.TC1, MS5611.SCL, R4.Pin_1, MCU1.pin_7
  N6: AMS_5915.TC2, MS5611.INT1, MS5611.SDA, R3.Pin_1, MCU1.pin_6
  N7: AMS_5915.TC3, MS5611.VDD, MS5611.PS, R4.Pin_0, R3.Pin_0, R1.Pin_1, MCU1.pin_27, C1.0
  N8: S2.Pin_3, S2.Pin_4, R5.Pin_1, MCU1.pin_26
  N9: R6.Pin_1, R7.Pin_1, MCU1.pin_1

custom parts:
  MPL3115A2: Altimeter/Pressure Sensor, I2C, 1.95V-3.6V supply, 50 to 110kPa
  Wemos Lolin32lite: Wemos Lolinlite32 wifi and blue tooth board based on the ESP-32 cpu, digital I/Os 19, analog inputs 6, clock 240mhz, Flash 4Mbytes, lipo battery charger (500ma connection broken out on breadboard but not pcb), usb.
